// Logisim project Multiprocesador.circ as structural Verilog: 1 circuit, main circuit Main
module Main (
);

  wire Encender_MIPS, Limpiar_RAM, MIPS_Escribir, Poder, Reloj, Usar_Little_Endian;
  wire [1:0] MIPS_Granularidad_Memoria;
  wire [7:0] RAM_Byte;
  wire [15:0] RAM_Nibble;
  wire [23:0] bit_extender_1_out;
  wire [25:0] bit_extender_2_out;
  wire [29:0] four_gb_address_endian_translator_1_word;
  wire [31:0] four_gb_address_endian_translator_2_byte, MIPS_Direccion_RAM, MIPS_Entrada_RAM,
       MIPS_Indice_Instruccion, RAM_Word, ROM_Word;

  // DipSwitch #(.number(3)) Opciones: pin names not known; wires that end beside it: Limpiar_RAM, Usar_Little_Endian, Poder
  Button u_Encender_MIPS (.out(Encender_MIPS));
  Clock u_Reloj (.out(Reloj));
  Four_GB_Address_Endian_Translator four_gb_address_endian_translator_1 (
    .Direccion_Big_Endian(MIPS_Indice_Instruccion), .Usar_Little_Endian(Usar_Little_Endian),
    .Word(four_gb_address_endian_translator_1_word));  // open: Byte, Nibble
  Four_GB_Address_Endian_Translator four_gb_address_endian_translator_2 (
    .Direccion_Big_Endian(MIPS_Direccion_RAM), .Usar_Little_Endian(Usar_Little_Endian),
    .Byte(four_gb_address_endian_translator_2_byte));  // open: Nibble, Word
  ROM #(.addrWidth(24), .dataWidth(32)) ROM_Memory (.addr(bit_extender_1_out), .data(ROM_Word));
  Bit_Extender #(.in_width(30), .out_width(24), .\type ("zero")) bit_extender_1 (
    .in(four_gb_address_endian_translator_1_word), .out(bit_extender_1_out));
  Bit_Extender #(.in_width(32), .out_width(26), .\type ("zero")) bit_extender_2 (
    .in(four_gb_address_endian_translator_2_byte), .out(bit_extender_2_out));
  MIPS_Processor Main_Processor (
    .Reloj(Reloj), .Poder(Poder), .Encender(Encender_MIPS), .Word_Instrucciones(ROM_Word),
    .Word_Datos(RAM_Word), .Nibble_Datos(RAM_Nibble), .Byte_Datos(RAM_Byte),
    .Direccion_Instrucciones(MIPS_Indice_Instruccion),
    .Bitmap_Granularidad_Memoria(MIPS_Granularidad_Memoria), .Escribir_Datos(MIPS_Escribir),
    .Direccion_Datos(MIPS_Direccion_RAM), .Valor_Escritura_Datos(MIPS_Entrada_RAM));
  Sixty_Four_Mebibyte_RAM_Controller RAM_Memory (
    .Direccion_Byte(bit_extender_2_out), .Entrada_Word(MIPS_Entrada_RAM),
    .Bitmap_Granularidad_Acceso(MIPS_Granularidad_Memoria), .Escribir(MIPS_Escribir), .Reloj(Reloj),
    .Limpiar(Limpiar_RAM), .Word(RAM_Word), .Nibble(RAM_Nibble), .Byte(RAM_Byte));

  // Notes on the sheet:
  //   Configuración
  //   Unidades de Memoria
  //   Procesadores
  //   contents of ROM_Memory (hex, n*v repeats v):
  //   20080001 21290002 1284822 8100000
endmodule
